# Fritzing sketch Arduino_ESP8266_NodeMCU_Access_Point_Web_Server_Led_RGB (saved by Fritzing 0.9.3b)
breadboards: 1

parts:
  U1 = NodeMCU V3.0
  LED1 = RGB LED - (4 legs) [package="5 mm [THT]"]
  R1 = Resistor [tolerance=±5% resistance=330 package=THT]
  R2 = Resistor [tolerance=±5% resistance=330 package=THT]
  R3 = Resistor [tolerance=±5% resistance=330 package=THT]

nets:
  N1: U1.D0, R1.Pin_1
  N2: U1.D1, R2.Pin_1
  N3: U1.D2, R3.Pin_1
  N4: U1.GND, LED1.common_anode
  N5: LED1.red_cathode, R1.Pin_0
  N6: LED1.green_cathode, R2.Pin_0
  N7: LED1.blue_cathode, R3.Pin_0

custom parts:
  NodeMCU V3.0: ESP8266 based NodeMCU
